// Logisim project miniRV.circ as structural Verilog: 9 circuits, main circuit main
module main (
  input  rst
);

  wire alu_1_wen, alu_1_wen_pc, clock_1_out;
  wire [1:0] dcdr_1_opcode, dcdr_1_rd, dcdr_1_rs1, dcdr_1_rs2;
  wire [3:0] dcdr_1_addr, dcdr_1_imm, pc_1_p_c;
  wire [7:0] alu_1_alu_out, instrrom_1_instruction, register_file_1_q1, register_file_1_q2;

  Clock clock_1 (.out(clock_1_out));
  pc pc_1 (.addr(dcdr_1_addr), .rst(rst), .clk(clock_1_out), .ext_wen(alu_1_wen_pc), .p_c(pc_1_p_c));
  instrROM instrrom_1 (.pc(pc_1_p_c), .Instruction(instrrom_1_instruction));
  dcdr dcdr_1 (
    .instruction(instrrom_1_instruction), .addr(dcdr_1_addr), .imm(dcdr_1_imm), .rs2(dcdr_1_rs2),
    .rs1(dcdr_1_rs1), .rd(dcdr_1_rd), .opcode(dcdr_1_opcode));
  alu alu_1 (
    .in_a(register_file_1_q1), .in_b(register_file_1_q2), .imm(dcdr_1_imm), .opcode(dcdr_1_opcode),
    .alu_out(alu_1_alu_out), .WEN(alu_1_wen), .WEN_PC(alu_1_wen_pc));
  register_file register_file_1 (
    .Data(alu_1_alu_out), .r2(dcdr_1_rs2), .rst(rst), .WEN(alu_1_wen), .clk(clock_1_out), .rd(dcdr_1_rd),
    .r1(dcdr_1_rs1), .Q2(register_file_1_q2), .Q1(register_file_1_q1));
endmodule

module Regx4 (
  input  [3:0] D,
  input  rst,
  input  WEN,
  input  clk,
  output [3:0] Q
);

  wire multiplexer_1_out, multiplexer_2_out, multiplexer_3_out, multiplexer_4_out;

  Multiplexer multiplexer_1 (.in0(Q[0]), .in1(D[0]), .out(multiplexer_1_out), .sel(WEN));
  Multiplexer multiplexer_2 (.in0(Q[1]), .in1(D[1]), .out(multiplexer_2_out), .sel(WEN));
  Multiplexer multiplexer_3 (.in0(Q[2]), .in1(D[2]), .out(multiplexer_3_out), .sel(WEN));
  Multiplexer multiplexer_4 (.in0(Q[3]), .in1(D[3]), .out(multiplexer_4_out), .sel(WEN));
  D_Flip_Flop d_ff_1 (.D(multiplexer_1_out), .clk(clk), .Q(Q[0]), .reset(rst));  // open: Qn, preset
  D_Flip_Flop d_ff_2 (.D(multiplexer_2_out), .clk(clk), .Q(Q[1]), .reset(rst));  // open: Qn, preset
  D_Flip_Flop d_ff_3 (.D(multiplexer_3_out), .clk(clk), .Q(Q[2]), .reset(rst));  // open: Qn, preset
  D_Flip_Flop d_ff_4 (.D(multiplexer_4_out), .clk(clk), .Q(Q[3]), .reset(rst));  // open: Qn, preset
endmodule

module Regx8 (
  input  [7:0] D,
  input  rst,
  input  WEN,
  input  clk,
  output [7:0] Q
);

  Regx4 regx4_1 (.D(D[3:0]), .rst(rst), .WEN(WEN), .clk(clk), .Q(Q[3:0]));
  Regx4 regx4_2 (.D(D[7:4]), .rst(rst), .WEN(WEN), .clk(clk), .Q(Q[7:4]));
endmodule

module pc (
  input  [3:0] addr,
  input  rst,
  input  clk,
  input  ext_wen,
  output [3:0] p_c
);

  wire [3:0] adder_1_out, multiplexer_1_out;

  Adder #(.width(4)) adder_1 (.a(4'b0001), .b(p_c), .out(adder_1_out));  // open: cin, cout
  Multiplexer #(.width(4)) multiplexer_1 (.in0(adder_1_out), .in1(addr), .out(multiplexer_1_out), .sel(ext_wen));
  Regx4 regx4_1 (.D(multiplexer_1_out), .rst(rst), .WEN(1'b1), .clk(clk), .Q(p_c));
endmodule

module register_file (
  input  [7:0] Data,
  input  [1:0] r2,
  input  rst,
  input  WEN,
  input  clk,
  input  [1:0] rd,
  input  [1:0] r1,
  output [7:0] Q2,
  output [7:0] Q1
);

  wire and_1_out, and_2_out, and_3_out, and_4_out, and_5_out, and_6_out, and_7_out, and_8_out, not_1_out,
       not_2_out;
  wire [7:0] regx8_1_q, regx8_2_q, regx8_3_q, regx8_4_q;

  not not_1 (not_1_out, rd[1]);
  not not_2 (not_2_out, rd[0]);
  and and_1 (and_1_out, not_1_out, not_2_out);
  and and_2 (and_2_out, rd[0], not_1_out);
  and and_3 (and_3_out, rd[1], not_2_out);
  and and_4 (and_4_out, rd[1], rd[0]);
  and and_5 (and_5_out, WEN, and_1_out);
  and and_6 (and_6_out, WEN, and_2_out);
  and and_7 (and_7_out, WEN, and_3_out);
  and and_8 (and_8_out, WEN, and_4_out);
  Regx8 regx8_1 (.D(Data), .rst(rst), .WEN(and_5_out), .clk(clk), .Q(regx8_1_q));
  Regx8 regx8_2 (.D(Data), .rst(rst), .WEN(and_6_out), .clk(clk), .Q(regx8_2_q));
  Regx8 regx8_3 (.D(Data), .rst(rst), .WEN(and_7_out), .clk(clk), .Q(regx8_3_q));
  Regx8 regx8_4 (.D(Data), .rst(rst), .WEN(and_8_out), .clk(clk), .Q(regx8_4_q));
  Multiplexer #(.select(2), .width(8)) multiplexer_1 (
    .in0(regx8_1_q), .in1(regx8_2_q), .in2(regx8_3_q), .in3(regx8_4_q), .out(Q2), .sel(r2));
  Multiplexer #(.select(2), .width(8)) multiplexer_2 (
    .in0(regx8_1_q), .in1(regx8_2_q), .in2(regx8_3_q), .in3(regx8_4_q), .out(Q1), .sel(r1));
endmodule

module dcdr (
  input  [7:0] instruction,
  output [3:0] addr,
  output [3:0] imm,
  output [1:0] rs2,
  output [1:0] rs1,
  output [1:0] rd,
  output [1:0] opcode
);

  wire not_1_out;
  wire [1:1] nand_1_out;

  Clock clock_1 ();  // open: out
  nand nand_1 (nand_1_out[1], instruction[6], instruction[7]);
  not not_1 (not_1_out, nand_1_out[1]);
  Multiplexer #(.width(2)) multiplexer_1 (.in0(instruction[3:2]), .in1({2{nand_1_out[1]}}), .out(rs1), .sel(not_1_out));

  assign addr = instruction[5:2];
  assign imm = instruction[3:0];
  assign opcode = instruction[7:6];
  assign rd = instruction[5:4];
  assign rs2 = instruction[1:0];
endmodule

module instrROM (
  input  [3:0] pc,
  output [7:0] Instruction
);

  Multiplexer #(.select(4), .width(8)) multiplexer_1 (
    .in0(8'h8a), .in1(8'h90), .in2(8'ha0), .in3(8'hb1), .in4(8'h17), .in5(8'h29), .in6(8'hd1), .in7(8'hdf),
    .out(Instruction), .sel(pc));  // open: in8, in9, in10, in11, in12, in13, in14, in15
endmodule

module alu (
  input  [7:0] in_a,
  input  [7:0] in_b,
  input  [3:0] imm,
  input  [1:0] opcode,
  output [7:0] alu_out,
  output WEN,
  output WEN_PC
);

  wire and_1_out, comparator_1_eq, not_1_out;
  wire [7:0] adder_1_out;

  Adder adder_1 (.a(in_a), .b(in_b), .out(adder_1_out));  // open: cin, cout
  Clock clock_1 ();  // open: out
  Multiplexer #(.width(8)) multiplexer_1 (.in0(adder_1_out), .in1({4'b0000, imm}), .out(alu_out), .sel(opcode[1]));
  Comparator comparator_1 (.a(in_b), .b(in_a), .eq(comparator_1_eq));  // open: gt, lt
  and and_1 (and_1_out, opcode[0], opcode[1]);
  not not_1 (not_1_out, comparator_1_eq);
  and and_2 (WEN_PC, not_1_out, and_1_out);
  not not_2 (WEN, and_1_out);
endmodule

module GPR (
  input  clk,
  input  [31:0] wdata,
  input  rst
);

  wire decoder_1_out1, decoder_1_out2, decoder_1_out3, decoder_1_out4, decoder_1_out5, decoder_1_out6,
       decoder_1_out7, decoder_1_out8, decoder_1_out9, decoder_1_out10, decoder_1_out11, decoder_1_out12,
       decoder_1_out13, decoder_1_out14, decoder_1_out15;
  wire [31:0] register_1_q, register_2_q, register_3_q, register_4_q, register_5_q, register_6_q,
       register_7_q, register_8_q, register_9_q, register_10_q, register_11_q, register_12_q, register_13_q,
       register_14_q, register_15_q, register_16_q;

  Decoder #(.select(4)) decoder_1 (
    .out1(decoder_1_out1), .out2(decoder_1_out2), .out3(decoder_1_out3), .out4(decoder_1_out4),
    .out5(decoder_1_out5), .out6(decoder_1_out6), .out7(decoder_1_out7), .out8(decoder_1_out8),
    .out9(decoder_1_out9), .out10(decoder_1_out10), .out11(decoder_1_out11), .out12(decoder_1_out12),
    .out13(decoder_1_out13), .out14(decoder_1_out14), .out15(decoder_1_out15));  // open: out0, sel, en
  Register #(.width(32)) register_1 (.D(wdata), .en(decoder_1_out1), .clk(clk), .Q(register_1_q));  // open: clr
  Register #(.width(32)) register_2 (.D(wdata), .en(decoder_1_out8), .clk(clk), .Q(register_2_q));  // open: clr
  Register #(.width(32)) register_3 (.D(wdata), .en(decoder_1_out1), .clk(clk), .Q(register_3_q));  // open: clr
  Register #(.width(32)) register_4 (.D(wdata), .en(decoder_1_out9), .clk(clk), .Q(register_4_q));  // open: clr
  Register #(.width(32)) register_5 (.D(wdata), .en(decoder_1_out2), .clk(clk), .Q(register_5_q));  // open: clr
  Register #(.width(32)) register_6 (.D(wdata), .en(decoder_1_out10), .clk(clk), .Q(register_6_q));  // open: clr
  Register #(.width(32)) register_7 (.D(wdata), .en(decoder_1_out3), .clk(clk), .Q(register_7_q));  // open: clr
  Register #(.width(32)) register_8 (.D(wdata), .en(decoder_1_out11), .clk(clk), .Q(register_8_q));  // open: clr
  Register #(.width(32)) register_9 (.D(wdata), .en(decoder_1_out4), .clk(clk), .Q(register_9_q));  // open: clr
  Register #(.width(32)) register_10 (.D(wdata), .en(decoder_1_out12), .clk(clk), .Q(register_10_q));  // open: clr
  Register #(.width(32)) register_11 (.D(wdata), .en(decoder_1_out5), .clk(clk), .Q(register_11_q));  // open: clr
  Register #(.width(32)) register_12 (.D(wdata), .en(decoder_1_out13), .clk(clk), .Q(register_12_q));  // open: clr
  Register #(.width(32)) register_13 (.D(wdata), .en(decoder_1_out6), .clk(clk), .Q(register_13_q));  // open: clr
  Register #(.width(32)) register_14 (.D(wdata), .en(decoder_1_out14), .clk(clk), .Q(register_14_q));  // open: clr
  Register #(.width(32)) register_15 (.D(wdata), .en(decoder_1_out7), .clk(clk), .Q(register_15_q));  // open: clr
  Register #(.width(32)) register_16 (.D(wdata), .en(decoder_1_out15), .clk(clk), .Q(register_16_q));  // open: clr
  Multiplexer #(.select(4), .width(32)) multiplexer_1 (
    .in0(register_1_q), .in1(register_3_q), .in2(register_5_q), .in3(register_7_q), .in4(register_9_q),
    .in5(register_11_q), .in6(register_13_q), .in7(register_15_q), .in8(register_2_q), .in9(register_4_q),
    .in10(register_6_q), .in11(register_8_q), .in12(register_10_q), .in13(register_12_q),
    .in14(register_14_q), .in15(register_16_q));  // open: out, sel
  Multiplexer #(.select(4), .width(32)) multiplexer_2 (
    .in0(register_1_q), .in1(register_3_q), .in2(register_5_q), .in3(register_7_q), .in4(register_9_q),
    .in5(register_11_q), .in6(register_13_q), .in7(register_15_q), .in8(register_2_q), .in9(register_4_q),
    .in10(register_6_q), .in11(register_8_q), .in12(register_10_q), .in13(register_12_q),
    .in14(register_14_q), .in15(register_16_q));  // open: out, sel
endmodule
