// Logisim project Full_Adder_counter.circ as structural Verilog: 3 circuits, main circuit main
module main (
  input  c_in,
  input  A,
  input  B,
  output Sum,
  output c_out
);

  wire and_1_out, and_2_out, xor_1_out;

  xor xor_1 (xor_1_out, A, B);
  xor xor_2 (Sum, c_in, xor_1_out);
  and and_1 (and_1_out, xor_1_out, c_in);
  and and_2 (and_2_out, A, B);
  or or_1 (c_out, and_1_out, and_2_out);
endmodule

module TwoBitAdder (
  input  c_in,
  input  [1:0] A,
  input  [1:0] B,
  output [1:0] Sum,
  output c_out
);

  wire main_1_c_out;

  main main_1 (.c_in(c_in), .A(A[0]), .B(B[0]), .Sum(Sum[0]), .c_out(main_1_c_out));
  main main_2 (.c_in(main_1_c_out), .A(A[1]), .B(B[1]), .Sum(Sum[1]), .c_out(c_out));
endmodule

module TwoBitCounter (
  input  in_1,
  input  [1:0] in_2,
  input  rst,
  output [1:0] out_4,
  output c_out
);

  wire clock_1_out;
  wire [1:0] twobitadder_1_sum;

  TwoBitAdder twobitadder_1 (.c_in(in_1), .A(out_4), .B(in_2), .Sum(twobitadder_1_sum), .c_out(c_out));
  Clock clock_1 (.out(clock_1_out));
  D_Flip_Flop d_ff_1 (.D(twobitadder_1_sum[1]), .clk(clock_1_out), .Q(out_4[1]), .reset(rst));  // open: Qn, preset
  D_Flip_Flop d_ff_2 (.D(twobitadder_1_sum[0]), .clk(clock_1_out), .Q(out_4[0]), .reset(rst));  // open: Qn, preset
endmodule
